# Fritzing sketch Audio_Connections (saved by Fritzing 1.0.0rc)

parts:
  Hat1 = Pisound Micro [package=THT]
  AMPHENOL_-_ACJS-MHDR_-_JACK_6_35MM2 = AMPHENOL - ACJS-MHDR [package=ACJS-MHDR]
  AMPHENOL_-_ACJS-MHDR_-_JACK_6_35MM3 = AMPHENOL - ACJS-MHDR [package=ACJS-MHDR]
  AMPHENOL_-_ACJS-MHDR_-_JACK_6_35MM4 = AMPHENOL - ACJS-MHDR [package=ACJS-MHDR]
  AMPHENOL_-_ACJS-MHDR_-_JACK_6_35MM5 = AMPHENOL - ACJS-MHDR [package=ACJS-MHDR]
  TRS2 = Audio Jack (TRS) 3.5mm [package="PG203J [THT]"]
  TRS1 = Audio Jack (TRS) 3.5mm [package="PG203J [THT]"]

nets:
  N1: Hat1.A01, TRS1.Sleeve
  N2: Hat1.A02, AMPHENOL_-_ACJS-MHDR_-_JACK_6_35MM2.Sleeve_(4)
  N3: Hat1.A03, TRS1.Tip
  N4: Hat1.A04, TRS1.Ring
  N5: Hat1.A05, AMPHENOL_-_ACJS-MHDR_-_JACK_6_35MM3.Sleeve_(4)
  N6: Hat1.A06, TRS2.Sleeve
  N7: Hat1.A07, AMPHENOL_-_ACJS-MHDR_-_JACK_6_35MM2.Ring_(5)
  N8: Hat1.A08, AMPHENOL_-_ACJS-MHDR_-_JACK_6_35MM3.Ring_(5)
  N9: Hat1.A09, AMPHENOL_-_ACJS-MHDR_-_JACK_6_35MM2.Tip_(6)
  N10: Hat1.A10, AMPHENOL_-_ACJS-MHDR_-_JACK_6_35MM3.Tip_(6)
  N11: Hat1.A11, AMPHENOL_-_ACJS-MHDR_-_JACK_6_35MM4.Sleeve_(4)
  N12: Hat1.A12, AMPHENOL_-_ACJS-MHDR_-_JACK_6_35MM5.Sleeve_(4)
  N13: Hat1.A13, AMPHENOL_-_ACJS-MHDR_-_JACK_6_35MM4.Ring_(5)
  N14: Hat1.A14, AMPHENOL_-_ACJS-MHDR_-_JACK_6_35MM5.Ring_(5)
  N15: Hat1.A15, AMPHENOL_-_ACJS-MHDR_-_JACK_6_35MM4.Tip_(6)
  N16: Hat1.A16, AMPHENOL_-_ACJS-MHDR_-_JACK_6_35MM5.Tip_(6)
  N17: Hat1.A17, TRS2.Tip
  N18: Hat1.A18, TRS2.Ring

notes:
  HP OUT
  LINE OUT LEFT
  LINE OUT RIGHT
  AUX IN
  LINE IN LEFT
  LINE IN RIGHT
