# Fritzing sketch Capless_HP (saved by Fritzing 1.0.0rc)

parts:
  Hat2 = Pisound Micro [package=THT]
  TRS2 = Audio Jack (TRS) 3.5mm [package="PG203J [THT]"]

nets:
  N1: Hat2.A01, TRS2.Sleeve
  N2: Hat2.A03, TRS2.Tip
  N3: Hat2.A04, TRS2.Ring

notes:
  CAPLESS HP OUT
