# Fritzing sketch Direct_Wire_RPi (saved by Fritzing 1.0.0rc)

parts:
  Hat1 = Pisound Micro [package=THT]
  Mod1 = Raspberry Pi 4B

nets:
  N1: Hat1.R01, Hat1.R17, Mod1.3V3
  N2: Hat1.R02, Hat1.R04, Mod1.5V
  N3: Hat1.R03, Mod1.GPIO2
  N4: Hat1.R05, Mod1.GPIO3
  N5: Hat1.R06, Hat1.R09, Hat1.R14, Hat1.R20, Hat1.R25, Hat1.R30, Hat1.R34, Hat1.R39, Mod1.GND
  N6: Hat1.R12, Mod1.GPIO18
  N7: Hat1.R35, Mod1.GPIO19
  N8: Hat1.R36, Mod1.GPIO16
  N9: Hat1.R37, Mod1.GPIO26
  N10: Hat1.R38, Mod1.GPIO20
  N11: Hat1.R40, Mod1.GPIO21
