# Fritzing sketch GPIO_Activity_LED (saved by Fritzing 1.0.0rc)
stripboards: 1

parts:
  Hat1 = Pisound Micro [package=THT]
  LED2 = LEDs [package=led10mm]
  LED3 = LEDs [package=led10mm]
  R1 = Resistor [tolerance=±5% power=0.25W resistance=220 package=THT]
  R2 = Resistor [tolerance=±5% power=0.25W resistance=220 package=THT]

nets:
  N1: Hat1.B02, LED2.C, LED3.C
  N2: Hat1.B03, R2.Pin_1
  N3: Hat1.B04, R1.Pin_1
  N4: LED2.A, R1.Pin_0
  N5: LED3.A, R2.Pin_0

notes:
  B04: GPIO
  B03: GPIO
  B02: GND
  A+
  C-
