# Fritzing sketch GPIO_Encoder (saved by Fritzing 1.0.0rc)

parts:
  Hat1 = Pisound Micro [package=THT]
  RE1 = Rotary Encoder [package=THT]

nets:
  N1: Hat1.B02, RE1.EncoderPinC
  N2: Hat1.B03, RE1.EncoderPinB
  N3: Hat1.B04, RE1.EncoderPinA

notes:
  B04: ENC GPIO
  B03: ENC GPIO
  B02: GND
