# Fritzing sketch GPIO_LED (saved by Fritzing 1.0.0rc)

parts:
  Hat1 = Pisound Micro [package=THT]
  LED1 = LEDs [package=led10mm]
  R1 = Resistor [tolerance=±5% power=0.25W resistance=220 package=THT]

nets:
  N1: Hat1.B02, LED1.C
  N2: Hat1.B03, R1.Pin_0
  N3: LED1.A, R1.Pin_1

notes:
  B02 (GND) <-> C (-)
  B03 (GPIO) <-> A (+)
