# Fritzing sketch GPIO_Potentiometer (saved by Fritzing 1.0.0rc)

parts:
  Hat1 = Pisound Micro [package=THT]
  R1 = Rotary Potentiometer (Small) [maximum_resistance=10kΩ knob_status=50% power=0.5W package=THT]

nets:
  N1: Hat1.B21, R1.leg2
  N2: Hat1.B22, R1.leg1
  N3: Hat1.B23, R1.wiper

notes:
  B21: AVDD
  B23: ADC GPIO
  B22: GND
