# Fritzing sketch GPIO_Switch (saved by Fritzing 1.0.0rc)

parts:
  Hat1 = Pisound Micro [package=THT]
  S1 = Pushbutton [package="[THT]"]

nets:
  N1: Hat1.B02, S1.Pin_3, S1.Pin_4
  N2: Hat1.B03, S1.Pin_1, S1.Pin_2

notes:
  B02: GND
  B03: GPIO
