# Fritzing sketch HP_Electrolytic_Caps (saved by Fritzing 1.0.0rc)

parts:
  Hat1 = Pisound Micro [package=THT]
  TRS1 = Audio Jack (TRS) 3.5mm [package="PG203J [THT]"]
  C2 = Electrolytic Capacitor [capacitance=0.47mF voltage=35V package="100 mil [THT, electrolytic]"]
  C3 = Electrolytic Capacitor [capacitance=1µF voltage=35V package="100 mil [THT, electrolytic]"]

nets:
  N1: Hat1.A02, TRS1.Sleeve
  N2: Hat1.A03, C2.+
  N3: Hat1.A04, C3.+
  N4: TRS1.Ring, C3.-
  N5: TRS1.Tip, C2.-

notes:
  HP OUT
  220µF ~ 470µF Electrolytic Caps
