# Fritzing sketch HP_Line_Out (saved by Fritzing 1.0.0rc)

parts:
  Hat1 = Pisound Micro [package=THT]
  C2 = Electrolytic Capacitor [capacitance=0.47mF voltage=35V package="100 mil [THT, electrolytic]"]
  C3 = Electrolytic Capacitor [capacitance=1µF voltage=35V package="100 mil [THT, electrolytic]"]
  AMPHENOL_-_ACJS-MHDR_-_JACK_6_35MM4 = AMPHENOL - ACJS-MHDR [package=ACJS-MHDR]

nets:
  N1: Hat1.A02, AMPHENOL_-_ACJS-MHDR_-_JACK_6_35MM4.Sleeve_(4)
  N2: Hat1.A03, C2.+
  N3: Hat1.A04, C3.+
  N4: C2.-, AMPHENOL_-_ACJS-MHDR_-_JACK_6_35MM4.Tip_(6)
  N5: C3.-, AMPHENOL_-_ACJS-MHDR_-_JACK_6_35MM4.Ring_(5)

notes:
  HP LINE OUT
  10µF ~ 100µF Electrolytic Caps
