# Fritzing sketch Line_Diffferential_Input (saved by Fritzing 1.0.0rc)

parts:
  Hat1 = Pisound Micro [package=THT]
  AMPHENOL_-_ACJS-MHDR_-_JACK_6_35MM4 = AMPHENOL - ACJS-MHDR [package=ACJS-MHDR]
  AMPHENOL_-_ACJS-MHDR_-_JACK_6_35MM5 = AMPHENOL - ACJS-MHDR [package=ACJS-MHDR]

nets:
  N1: Hat1.A11, AMPHENOL_-_ACJS-MHDR_-_JACK_6_35MM5.Sleeve_(4)
  N2: Hat1.A12, AMPHENOL_-_ACJS-MHDR_-_JACK_6_35MM4.Sleeve_(4)
  N3: Hat1.A13, AMPHENOL_-_ACJS-MHDR_-_JACK_6_35MM5.Ring_(5)
  N4: Hat1.A14, AMPHENOL_-_ACJS-MHDR_-_JACK_6_35MM5.Tip_(6)
  N5: Hat1.A15, AMPHENOL_-_ACJS-MHDR_-_JACK_6_35MM4.Ring_(5)
  N6: Hat1.A16, AMPHENOL_-_ACJS-MHDR_-_JACK_6_35MM4.Tip_(6)

notes:
  LINE IN LEFT
  LINE IN RIGHT
