# Fritzing sketch Line_MicBias_Electret_Input (saved by Fritzing 1.0.0rc)
stripboards: 2

parts:
  Hat1 = Pisound Micro [package=THT]
  U2 = MIC [package=mic-9.7mm]
  U3 = MIC [package=mic-9.7mm]

nets:
  N1: Hat1.A12, Hat1.A13, U3.2
  N2: Hat1.A14, U3.1
  N3: Hat1.A15, Hat1.A20, U2.1
  N4: Hat1.A16, U2.2

notes:
  ELECTRET MICS
  MICBIAS ENABLED
