# Fritzing sketch Line_Single_Ended_Input (saved by Fritzing 1.0.0rc)

parts:
  Hat1 = Pisound Micro [package=THT]
  J1 = 1/4 inch mono jack [package=audio-jack-6.5mm-panel-mount]
  J2 = 1/4 inch mono jack [package=audio-jack-6.5mm-panel-mount]
  J3 = 1/4 inch mono jack [package=audio-jack-6.5mm-panel-mount]
  J4 = 1/4 inch mono jack [package=audio-jack-6.5mm-panel-mount]

nets:
  N1: Hat1.A11, J1.Sleeve
  N2: Hat1.A12, J2.Sleeve
  N3: Hat1.A13, J1.Tip
  N4: Hat1.A14, J2.Tip
  N5: Hat1.A15, J3.Tip
  N6: Hat1.A16, J4.Tip
  N7: Hat1.A19, J4.Sleeve
  N8: Hat1.A20, J3.Sleeve

notes:
  SE1
  SINGLE ENDED INPUTS
  SE2
  SE3
  SE4

custom parts:
  1/4 inch mono jack: 1/4 inch mono Audio Jack Simple 1/4 inch panel mount audio jack.
