# Fritzing sketch Line_Single_Ended_Output (saved by Fritzing 1.0.0rc)

parts:
  Hat1 = Pisound Micro [package=THT]
  AMPHENOL_-_ACJS-MHDR_-_JACK_6_35MM5 = AMPHENOL - ACJS-MHDR [package=ACJS-MHDR]

nets:
  N1: Hat1.A06, AMPHENOL_-_ACJS-MHDR_-_JACK_6_35MM5.Sleeve_(4)
  N2: Hat1.A08, AMPHENOL_-_ACJS-MHDR_-_JACK_6_35MM5.Tip_(6)
  N3: Hat1.A10, AMPHENOL_-_ACJS-MHDR_-_JACK_6_35MM5.Ring_(5)

notes:
  STEREO LINE OUT
