# Fritzing sketch MIDI_Connections (saved by Fritzing 1.0.0rc)

parts:
  Hat1 = Pisound Micro [package=THT]
  U1 = MIDI_CONN_FEMALE [package=din_5_female]
  U2 = MIDI_CONN_FEMALE [package=din_5_female]
  LED1 = LEDs [package=led10mm]
  R1 = Resistor [tolerance=±5% power=0.25W resistance=1000 package=THT]
  LED2 = LEDs [package=led10mm]
  R2 = Resistor [tolerance=±5% power=0.25W resistance=1000 package=THT]

nets:
  N1: Hat1.A20, LED1.C
  N2: Hat1.A21, U1.MIDI_IN
  N3: Hat1.A22, U1.MIDI_OUT
  N4: Hat1.A23, U2.MIDI_IN
  N5: Hat1.A24, U2.MIDI_OUT
  N6: Hat1.A25, U2.NC1
  N7: Hat1.A26, LED2.C
  N8: Hat1.A27, R1.Pin_1
  N9: Hat1.A28, R2.Pin_1
  N10: LED1.A, R1.Pin_0
  N11: LED2.A, R2.Pin_0

notes:
  MIDI INPUT
  MIDI OUTPUT
  C -
  A +
